# Fritzing sketch DiagramaSensorGestos (saved by Fritzing 0.9.3b)
breadboards: 1

parts:
  Componente1 = Logic Level Converter
  Componente2 = Arduino Uno (Rev3)
  J1 = female pin header, 6 pins [form="♀ (female)"]

nets:
  N1: Componente1.TX2_LV, J1.pin4
  N2: Componente1.RX2_LV, J1.pin5
  GND: Componente1.GND, Componente2.GND, J1.pin2
  N3: Componente1.LV, Componente2.3V3, J1.pin3
  N4: Componente1.RX_LV, J1.pin6
  N5: Componente1.RX_HV, Componente2.D2
  N6: Componente1.HV, Componente2.5V
  N7: Componente1.RX2_HV, Componente2.A5/SCL
  N8: Componente1.TX2_HV, Componente2.A4/SDA
